// Logisim project ex5.circ as structural Verilog: 1 circuit, main circuit main
module main (
  input  A,
  input  B,
  input  C,
  input  D,
  output Z,
  output Y
);

  wire and_1_out, and_2_out, and_3_out, not_1_out, not_2_out;

  not not_1 (not_1_out, B);
  not not_2 (not_2_out, C);
  and and_1 (and_1_out, A, not_1_out, C);
  and and_2 (and_2_out, B, D);
  and and_3 (and_3_out, A, not_2_out, D);
  or or_1 (Z, and_3_out, and_2_out);
  or or_2 (Y, and_1_out, D);
endmodule
